// Logisim project 4 Bit Adder(2).circ as structural Verilog: 1 circuit, main circuit main
module main (
  input  [3:0] A_in_4,
  input  [3:0] B_in_4,
  input  Carry_in,
  output Carry_out,
  output Out_4
);

  wire main_1_sum_out, main_2_carry_out, main_2_sum_out, main_3_carry_out, main_3_sum_out, main_4_carry_out;

  Full_Adder_main main_1 (
    .Carry_in(main_2_carry_out), .A_in(A_in_4[3]), .B_in(B_in_4[3]), .Sum_out(main_1_sum_out),
    .Carry_out(Carry_out));
  Full_Adder_main main_2 (
    .Carry_in(main_3_carry_out), .A_in(A_in_4[2]), .B_in(B_in_4[2]), .Sum_out(main_2_sum_out),
    .Carry_out(main_2_carry_out));
  Full_Adder_main main_3 (
    .Carry_in(main_4_carry_out), .A_in(A_in_4[1]), .B_in(B_in_4[1]), .Sum_out(main_3_sum_out),
    .Carry_out(main_3_carry_out));
  Full_Adder_main main_4 (
    .Carry_in(Carry_in), .A_in(B_in_4[0]), .B_in(A_in_4[0]), .Sum_out(Out_4), .Carry_out(main_4_carry_out));
endmodule
