// Logisim project Full Adder.circ as structural Verilog: 1 circuit, main circuit main
module main (
  input  Carry_in,
  input  A_in,
  input  B_in,
  output Sum_out,
  output Carry_out
);

  wire main_1_carry_out, main_1_sum_out, main_2_carry_out;

  half_adder_main main_1 (.a_in(A_in), .b_in(B_in), .Sum_out(main_1_sum_out), .Carry_out(main_1_carry_out));
  half_adder_main main_2 (.a_in(Carry_in), .b_in(main_1_sum_out), .Sum_out(Sum_out), .Carry_out(main_2_carry_out));
  or or_1 (Carry_out, main_2_carry_out, main_1_carry_out);
endmodule
