// Logisim project MyXOR.circ as structural Verilog: 1 circuit, main circuit main
module main (
  input  a,
  input  b,
  output \output 
);

  wire nand_1_out, or_1_out;

  or or_1 (or_1_out, a, b);
  nand nand_1 (nand_1_out, a, b);
  and and_1 (\output , or_1_out, nand_1_out);
endmodule
