// Logisim project half-adder.circ as structural Verilog: 1 circuit, main circuit main
module main (
  input  a_in,
  input  b_in,
  output Sum_out,
  output Carry_out
);

  xor xor_1 (Sum_out, a_in, b_in);
  and and_1 (Carry_out, a_in, b_in);
endmodule
